# Fritzing sketch RocketUAVSensorModule (saved by Fritzing 0.9.10b)
circuit board: 5.19999cm x 5.19999cm
breadboards: 1

parts:
  BattMon_A3 = female pin header, 1 pin [form="♀ (female)"]
  Baro1 = female pin header, 6 pins [form="♀ (female)"]
  Accel = female pin header, 8 pins [form="♀ (female)"]
  J3 = female pin header, 5 pins [form="♀ (female)"]
  J4 = female pin header, 5 pins [form="♀ (female)"]
  Baro2 = female pin header, 6 pins [form="♀ (female)"]
  G_V_D_C = female pin header, 4 pins [form="♀ (female)"]
  PAM = female pin header, 5 pins [form="♀ (female)"]
  R3 = Resistor [tolerance=±5% power=0.25 resistance=10k package=THT]
  R2 = Resistor [tolerance=±5% power=0.25 resistance=10k package=THT]
  R1 = Resistor [tolerance=±5% power=0.25 resistance=4.7k package=THT]
  3-6V_G = female pin header, 2 pins [form="♀ (female)"]

nets:
  N1: BattMon_A3.pin1, J3.pin3
  N2: Baro1.pin1, Accel.pin2, J4.pin1, Baro2.pin6, G_V_D_C.pin2, R1.Pin_1
  N3: Baro1.pin2, Accel.pin1, J3.pin2, Baro2.pin5, G_V_D_C.pin1, PAM.pin2, PAM.pin5, R3.Pin_0, 3-6V_G.pin1
  N4: Baro1.pin3, Accel.pin8, J4.pin2, Baro2.pin4, G_V_D_C.pin4
  N5: Baro1.pin4, Accel.pin7, J4.pin4, Baro2.pin3, G_V_D_C.pin3
  N6: J3.pin1, PAM.pin4, R2.Pin_0, 3-6V_G.pin2
  N7: J3.pin4, R3.Pin_1, R2.Pin_1
  N8: J4.pin3, PAM.pin1
  N9: Baro2.pin1, R1.Pin_0

notes:
  Face Up
  0x76
  V+
  3V3 SCL A0 SDA Vbus
  0x53
  SC SD  -   -   -   V+  G
  A+ A- - V+ G
  0x77
  Mike Loman 2025
  Sensor Module
  Face Down
  Rst A3 A2 Gnd Batt
  M0 Trinket
  Bat Gnd
  RocketUAV
